# Fritzing sketch Prototipação - Projeto 1 (saved by Fritzing 0.9.3b)
breadboards: 1

parts:
  Componente1 = Arduino Uno (Rev3)
  LED4 = LED - 5mm [color="Red (633nm)" package="5 mm [THT]"]
  R3 = Resistor [tolerance=±5% resistance=220 package=THT]

nets:
  N1: Componente1.D13/SCK, R3.Pin_0
  N2: Componente1.GND, LED4.cathode
  N3: LED4.anode, R3.Pin_1
