# Fritzing sketch Prototipação - Projeto 1.1 (saved by Fritzing 0.9.3b)
breadboards: 1

parts:
  LED1 = LED - 5mm [color="Red (633nm)" package="5 mm [THT]"]
  LED2 = LED - 5mm [color="Red (633nm)" package="5 mm [THT]"]
  LED3 = LED - 5mm [color="Red (633nm)" package="5 mm [THT]"]
  LED4 = LED - 5mm [color="Yellow (595nm)" package="5 mm [THT]"]
  LED5 = LED - 5mm [color="Yellow (595nm)" package="5 mm [THT]"]
  LED6 = LED - 5mm [color="Yellow (595nm)" package="5 mm [THT]"]
  LED7 = LED - 5mm [color="Green (555nm)" package="5 mm [THT]"]
  LED9 = LED - 5mm [color="Green (555nm)" package="5 mm [THT]"]
  LED8 = LED - 5mm [color="Green (555nm)" package="5 mm [THT]"]
  Componente1 = Arduino Mega 2560 (Rev3)
  R10 = Resistor [tolerance=±10% resistance=220 package=THT]
  R11 = Resistor [tolerance=±5% resistance=220 package=THT]
  R13 = Resistor [tolerance=±5% resistance=220 package=THT]
  R12 = Resistor [tolerance=±5% resistance=220 package=THT]
  R17 = Resistor [tolerance=±5% resistance=220 package=THT]
  R15 = Resistor [tolerance=±5% resistance=220 package=THT]
  R16 = Resistor [tolerance=±5% resistance=220 package=THT]
  R14 = Resistor [tolerance=±5% resistance=220 package=THT]
  R18 = Resistor [tolerance=±5% resistance=220 package=THT]

nets:
  N1: LED1.cathode, LED2.cathode, LED3.cathode, LED4.cathode, LED5.cathode, LED6.cathode, LED7.cathode, LED9.cathode, LED8.cathode, Componente1.GND
  N2: LED1.anode, R16.Pin_1
  N3: LED2.anode, R12.Pin_1
  N4: LED3.anode, R10.Pin_1
  N5: LED4.anode, R14.Pin_1
  N6: LED5.anode, R17.Pin_1
  N7: LED6.anode, R11.Pin_1
  N8: LED7.anode, R15.Pin_1
  N9: LED9.anode, R18.Pin_1
  N10: LED8.anode, R13.Pin_1
  N11: Componente1.D13_PWM, R10.Pin_0
  N12: Componente1.D12_PWM, R11.Pin_0
  N13: Componente1.D11_PWM, R13.Pin_0
  N14: Componente1.D10_PWM, R12.Pin_0
  N15: Componente1.D9_PWM, R17.Pin_0
  N16: Componente1.D8_PWM, R15.Pin_0
  N17: Componente1.D5_PWM, R18.Pin_0
  N18: Componente1.D6_PWM, R14.Pin_0
  N19: Componente1.D7_PWM, R16.Pin_0

// code stored in the sketch: Codigo-Fonte_Projeto1.1.ino
void setup() {
  //Definindo as Portas e os parâmetros das mesmas

  //Semaforo (Rua) [SR]
  pinMode(13, OUTPUT); // Vermelho
  pinMode(12, OUTPUT); // Amarelo
  pinMode(11, OUTPUT); // Verde

  //Semaforo 1 (Avenida) [S1A]
  pinMode(10, OUTPUT); // Vermelho
  pinMode(9, OUTPUT); // Amarelo
  pinMode(8, OUTPUT); // Verde
  
  //Semaforo 2 (Avenida) [S2A]
  pinMode(7, OUTPUT); // Vermelho
  pinMode(6, OUTPUT); // Amarelo
  pinMode(5, OUTPUT); // Verde

}

void loop() {

  //Estado: [SR]:Verde | [S12A]:Vermelho
  digitalWrite(11, HIGH); // [SR] -> Liga Verde
  digitalWrite(10, HIGH); // [S1A] -> Liga Vermelho
  digitalWrite(7, HIGH); // [S2A] -> Liga Vermelho

  //Estado: [SR]:Amarelo | [S12A]:Vermelho 
  delay(5000);
  digitalWrite(11, LOW); // [SR] -> Desliga Verde 
  digitalWrite(12, HIGH); // [SR] -> Liga Amarelo

  //Estado: [SR]:Vermelho | [S12A]:Verde
  delay(2000);
  digitalWrite(12, LOW); // [SR] -> Desliga Amarelo
  digitalWrite(10, LOW); // [S1A] -> Desliga Verde
  digitalWrite(7, LOW); // [S2A] -> Desliga Verde
  digitalWrite(13, HIGH); // [SR] -> Liga Vermelho
  digitalWrite(8, HIGH); // [S1A] -> Liga Verde
  digitalWrite(5, HIGH); // [S2A] -> Liga Verde
  
  //Estado: [SR]:Vermelho | [S12A]:Amarelo
  delay(5000);
  digitalWrite(8, LOW); // [S1A] -> Desliga Verde 
  digitalWrite(5, LOW); // [S2A] -> Desliga Verde
  digitalWrite(9, HIGH); // [S1A] -> Liga Amarelo
  digitalWrite(6, HIGH); // [S2A] -> Liga Amarelo

  //Estado: Limpano para o novo Ciclo
  delay(2000);
  digitalWrite(13, LOW); // [SR] -> Desliga Vermelho
  digitalWrite(9, LOW); // [S1A] -> Desliga Amarelo
  digitalWrite(6, LOW); // [S2A] -> Desliga Amarelo
 
  }
