# Fritzing sketch Prototipação - Projeto 1.1 (saved by Fritzing 0.9.3b)
breadboards: 1

parts:
  Componente1 = Arduino Uno (Rev3)
  LED2 = LED - 5mm [color="Red (633nm)" package="5 mm [THT]"]
  LED3 = LED - 5mm [color="Yellow (595nm)" package="5 mm [THT]"]
  LED4 = LED - 5mm [color="Green (555nm)" package="5 mm [THT]"]
  R1 = Resistor [tolerance=±5% resistance=220 package=THT]
  R2 = Resistor [tolerance=±5% resistance=220 package=THT]
  R3 = Resistor [tolerance=±5% resistance=220 package=THT]

nets:
  N1: Componente1.D13/SCK, R1.Pin_0
  N2: Componente1.GND, LED2.cathode, LED3.cathode, LED4.cathode
  N3: Componente1.D4, R3.Pin_0
  N4: Componente1.D7, R2.Pin_0
  N5: LED2.anode, R1.Pin_1
  N6: LED3.anode, R2.Pin_1
  N7: LED4.anode, R3.Pin_1
