# Fritzing sketch Prototipação - Projeto 10 (saved by Fritzing 0.9.3b)
breadboards: 1

parts:
  Componente1 = Arduino Uno (Rev3)
  WeMos_D1_Mini_Relay_Shield_V1 = WeMos D1 Mini Relay Shield V2
  LED1 = LED - 5mm [color="Red (633nm)" package="5 mm [THT]"]
  R1 = Resistor [tolerance=±5% resistance=220 package="0603 [SMD]"]

nets:
  N1: Componente1.D13/SCK, WeMos_D1_Mini_Relay_Shield_V1.D1
  N2: Componente1.GND, WeMos_D1_Mini_Relay_Shield_V1.COM, WeMos_D1_Mini_Relay_Shield_V1.G
  5V: Componente1.5V, WeMos_D1_Mini_Relay_Shield_V1.5V, R1.Pin_0
  N3: WeMos_D1_Mini_Relay_Shield_V1.NO, LED1.cathode
  N4: LED1.anode, R1.Pin_1
