# Fritzing sketch Prototipação - Projeto 3 (saved by Fritzing 0.9.3b)

parts:
  SG3 = Buzzer 12mm [package=buzzer-12mm-ns]
  Componente1 = Arduino Uno (Rev3)

nets:
  N1: SG3.1, Componente1.D10_PWM/SS
  N2: SG3.2, Componente1.GND
