# Fritzing sketch Prototipação - Projeto 4 (saved by Fritzing 0.9.3b)
breadboards: 1

parts:
  T1 = LM35 Temperature Sensor [package="TO92 [THT]"]
  Componente1 = Arduino Uno (Rev3)
  SG1 = Buzzer 12mm [package=buzzer-12mm-ns]

nets:
  N1: T1.+Vs, Componente1.5V
  N2: T1.Vout, Componente1.D2
  GND: T1.GND, Componente1.GND, SG1.1
  N3: Componente1.D13/SCK, SG1.2
