# Fritzing sketch Prototipação - Projeto 4.1 (saved by Fritzing 0.9.3b)

parts:
  Componente1 = Arduino Uno (Rev3)
  SG1 = Buzzer 12mm [package=buzzer-12mm-ns]

nets:
  N1: Componente1.D13/SCK, SG1.1
  N2: Componente1.GND, SG1.2
