# Fritzing sketch Prototipação - Projeto 4.1 (saved by Fritzing 0.9.3b)
breadboards: 1

parts:
  Componente1 = Arduino Uno (Rev3)
  SG1 = Buzzer 12mm [package=buzzer-12mm-ns]
  DHT1 = DHT11 Humitidy and Temperature Sensor

nets:
  N1: Componente1.D13/SCK, SG1.2
  N2: Componente1.D2, DHT1.DATA
  5V: Componente1.5V, DHT1.VDD
  GND: Componente1.GND, SG1.1, DHT1.GND

custom parts:
  DHT11 Humitidy and Temperature Sensor: DHT11 Humidity and Temperature Sensor
