# Fritzing sketch Prototipação Projeto 5 - Botao (saved by Fritzing 0.9.3b)
breadboards: 1

parts:
  S1 = Momentary Switch [package=ksa_sealed_tac_switch]
  Componente1 = Arduino Uno (Rev3)
  R1 = Resistor [tolerance=±5% resistance=220 package="0402 [SMD]"]
  LED1 = LED - 3mm [color="Red (633nm)" package="3 mm [THT]"]  # not connected

nets:
  N1: S1.2, Componente1.D7, R1.Pin_0
  N2: S1.4, Componente1.5V
  N3: Componente1.GND, R1.Pin_1
