# Fritzing sketch Prototipação - Projeto 6 (saved by Fritzing 0.9.3b)
breadboards: 1

parts:
  Componente1 = Arduino Uno (Rev3)
  R1 = Photocell (LDR) [package=THT]
  R2 = Resistor [tolerance=±5% resistance=220 package=THT]

nets:
  N1: Componente1.A0, R1.pin_1, R2.Pin_0
  N2: Componente1.GND, R2.Pin_1
  N3: Componente1.5V, R1.pin_0
