# Fritzing sketch Prototipação Projeto 6.3 - LDR com 3 Leds (saved by Fritzing 0.9.3b)
breadboards: 1

parts:
  Componente1 = Arduino Uno (Rev3)
  R1 = Photocell (LDR) [package=THT]
  R2 = Resistor [tolerance=±5% resistance=220 package=THT]
  LED1 = smd LED [color="Red (633nm)" package="0805 [SMD]"]
  LED2 = smd LED [color="Green (565nm)" package="0805 [SMD]"]
  LED3 = smd LED [color="Yellow (592nm)" package="0805 [SMD]"]
  R3 = Resistor [tolerance=±5% resistance=220 package=THT]
  R4 = Resistor [tolerance=±5% resistance=220 package=THT]
  R5 = Resistor [tolerance=±5% resistance=220 package=THT]

nets:
  N1: Componente1.D12/MISO, R2.Pin_0
  N2: Componente1.D2, R5.Pin_0
  N3: Componente1.D4, R4.Pin_0
  N4: Componente1.5V, R1.pin_0
  N5: Componente1.GND, LED1.cathode, LED2.cathode, LED3.cathode, R3.Pin_1
  N6: R1.pin_1, R3.Pin_0
  N7: R2.Pin_1, LED3.anode
  N8: LED1.anode, R5.Pin_1
  N9: LED2.anode, R4.Pin_1
