# Fritzing sketch Prototipação - Projeto 6.1 (saved by Fritzing 0.9.3b)
breadboards: 1

parts:
  Componente1 = Arduino Uno (Rev3)
  R1 = Photocell (LDR) [package=THT]
  R2 = Resistor [tolerance=±5% resistance=220 package=THT]
  LED1 = LED - 5mm [color="Yellow (595nm)" package="5 mm [THT]"]
  R3 = Resistor [tolerance=±5% resistance=220 package=THT]

nets:
  N1: Componente1.A0, R1.pin_1, R2.Pin_0
  N2: Componente1.D13/SCK, R3.Pin_0
  N3: Componente1.GND, R2.Pin_1, LED1.cathode
  N4: Componente1.5V, R1.pin_0
  N5: LED1.anode, R3.Pin_1
