# Fritzing sketch Prototipação - Projeto 7.1 Ultrasonic com Buzzer (saved by Fritzing 0.9.3b)
breadboards: 1

parts:
  hc-sr1 = hc-sr04
  Componente1 = Arduino Mega 2560 (Rev3)
  SG1 = Buzzer 12mm [package=buzzer-12mm-ns]

nets:
  VCC: hc-sr1.VCC, Componente1.5V
  N1: hc-sr1.Trig, Componente1.D12_PWM
  N2: hc-sr1.Echo, Componente1.D13_PWM
  GND: hc-sr1.GND, Componente1.GND, SG1.1
  N3: Componente1.D10_PWM, SG1.2
