# Fritzing sketch Prototipação - Projeto 7 (saved by Fritzing 0.9.3b)
breadboards: 1

parts:
  hc-sr1 = hc-sr04
  Componente1 = Arduino Mega 2560 (Rev3)

nets:
  VCC: hc-sr1.VCC, Componente1.5V
  N1: hc-sr1.Trig, Componente1.D12_PWM
  N2: hc-sr1.Echo, Componente1.D13_PWM
  GND: hc-sr1.GND, Componente1.GND

// code stored in the sketch: Prototipaτπo - Projeto 7.ino
EU NAO SEI
