# Fritzing sketch Prototipação - Projeto 8 (saved by Fritzing 0.9.3b)

parts:
  Componente1 = Arduino Uno (Rev3)
  PIR1 = PIR sensor

nets:
  N1: Componente1.D13/SCK, PIR1.SIG
  5V: Componente1.5V, PIR1.VDD
  GND: Componente1.GND, PIR1.GND
