# Fritzing sketch Prototipação - Projeto 9 - Sensor Óptico (saved by Fritzing 0.9.3b)

parts:
  Componente1 = Arduino Uno (Rev3)
  TCRT1 = TCRT5000 sensor module [part_number=151608]

nets:
  N1: Componente1.D13/SCK, TCRT1.T+
  N2: Componente1.GND, TCRT1.D-, TCRT1.T-
  N3: Componente1.5V, TCRT1.D+

custom parts:
  TCRT5000 sensor module: breakout board with TCRT5000
